// Logisim project healthy.circ as structural Verilog: 7 circuits, main circuit main
module main (
);

  wire button_1_out, button_2_out, undriven;
  wire [3:0] counter_out_3;
  wire [7:0] ram_1_data, rom_1_data;

  Button button_1 (.out(button_1_out));
  Button button_2 (.out(button_2_out));
  counter counter (.in_1(button_1_out), .out_3(counter_out_3), .in_2(button_2_out));
  ROM #(.addrWidth(4)) rom_1 (.addr(counter_out_3), .data(rom_1_data));  // open: sel
  RAM #(.addrWidth(4), .bus("separate")) ram_1 (
    .data(ram_1_data), .clk(undriven), .clr(button_2_out));  // open: addr, din, str, sel, ld

  // Notes on the sheet:
  //   count
  //   clear
  //   instruks rom
  //   controller unit
  //   contents of rom_1 (hex, n*v repeats v):
  //   85 97 b1 81 94 a1
  //   instrukser
  //   data forgrener
  //   data ut
  //   posisjon
  //   data inn
  //   R: register
  //   data ut
endmodule

module counter (
  input  in_1,
  input  in_2,
  output [3:0] out_3
);

  wire adder_1_cout, and_1_out, not_1_out;
  wire [3:0] adder_1_out;

  Register #(.width(4)) register_1 (.D(adder_1_out), .Q(out_3), .clk(and_1_out), .clr(in_2));  // open: en
  and and_1 (and_1_out, in_1, not_1_out);
  not not_1 (not_1_out, adder_1_cout);
  Adder #(.width(4)) adder_1 (.a(out_3), .b(4'b0001), .out(adder_1_out), .cout(adder_1_cout));  // open: cin
endmodule

module _2x4_tristate (
  input  in_1,
  input  [3:0] in,
  input  [3:0] in_3,
  input  in_4,
  output [3:0] out_5,
  output [3:0] out_6
);

  assign out_5 = in_1 ? in : 4'bz;  // Controlled_Buffer controlled_buffer_1
  assign out_6 = in_4 ? in_3 : 4'bz;  // Controlled_Buffer controlled_buffer_2

  // Notes on the sheet:
  //   out
endmodule

module _2_1_mux (
  input  [3:0] in_1,
  input  [3:0] in_2,
  input  in_3,
  output [3:0] out_4
);

  wire not_1_out;

  not not_1 (not_1_out, in_3);
  _2x4_tristate u_2x4_tristate_1 (.in(in_1), .in_3(in_2), .in_1(not_1_out), .in_4(in_3), .out_5(out_4), .out_6(out_4));
endmodule

module ram (
  input  [3:0] skriv,
  input  [3:0] in_2,
  input  in_3,
  output [3:0] les
);

  wire not_1_out;
  wire [3:0] ram_1_data;

  RAM #(.addrWidth(4), .dataWidth(4), .bus("asynch")) ram_1 (
    .addr(in_2), .data(ram_1_data), .sel(1'b1), .ld(in_3));  // open: clr
  assign ram_1_data = not_1_out ? skriv : 4'bz;  // Controlled_Buffer controlled_buffer_1
  not not_1 (not_1_out, in_3);
  assign les = in_3 ? ram_1_data : 4'bz;  // Controlled_Buffer controlled_buffer_2

  // Notes on the sheet:
  //   posisjon i minne
  //   operasjon skriv/les
endmodule

module instrukser (
  input  [3:0] in_1,
  input  in_2,
  output [7:0] out_3
);

  ROM #(.addrWidth(4)) rom_1 (.addr(in_1), .data(out_3), .sel(in_2));
endmodule

module dekoder (
  input  [3:0] in_1,
  input  clock
);


  // Notes on the sheet:
  //   signal in
endmodule
